// Logisim project Counter3Bit.circ as structural Verilog
module Counter_3bit (
);

  wire and_1_out, and_2_out, and_3_out, and_4_out, and_5_out, and_6_out, and_7_out, and_8_out, clock_1_out,
       counterflipflop_1_b0, counterflipflop_1_b1, counterflipflop_1_b2, counterflipflop_2_b0,
       counterflipflop_2_b1, counterflipflop_2_b2, counterflipflop_3_b0, counterflipflop_3_b1,
       counterflipflop_3_b2, counterflipflop_4_b0, counterflipflop_4_b1, counterflipflop_4_b2,
       counterflipflop_5_b0, counterflipflop_5_b1, counterflipflop_5_b2, counterflipflop_6_b0,
       counterflipflop_6_b1, counterflipflop_6_b2, counterflipflop_7_b0, counterflipflop_7_b1,
       counterflipflop_7_b2, counterflipflop_8_b0, counterflipflop_8_b1, counterflipflop_8_b2;

  Clock clock_1 (.out(clock_1_out));
  CounterFlipFlop counterflipflop_1 (
    .Clock(clock_1_out), .b2(counterflipflop_1_b2), .b1(counterflipflop_1_b1), .b0(counterflipflop_1_b0));
  CounterFlipFlop counterflipflop_2 (
    .Clock(clock_1_out), .b2(counterflipflop_2_b2), .b1(counterflipflop_2_b1), .b0(counterflipflop_2_b0));
  CounterFlipFlop counterflipflop_3 (
    .Clock(clock_1_out), .b2(counterflipflop_3_b2), .b1(counterflipflop_3_b1), .b0(counterflipflop_3_b0));
  CounterFlipFlop counterflipflop_4 (
    .Clock(clock_1_out), .b2(counterflipflop_4_b2), .b1(counterflipflop_4_b1), .b0(counterflipflop_4_b0));
  CounterFlipFlop counterflipflop_5 (
    .Clock(clock_1_out), .b2(counterflipflop_5_b2), .b1(counterflipflop_5_b1), .b0(counterflipflop_5_b0));
  CounterFlipFlop counterflipflop_6 (
    .Clock(clock_1_out), .b2(counterflipflop_6_b2), .b1(counterflipflop_6_b1), .b0(counterflipflop_6_b0));
  CounterFlipFlop counterflipflop_7 (
    .Clock(clock_1_out), .b2(counterflipflop_7_b2), .b1(counterflipflop_7_b1), .b0(counterflipflop_7_b0));
  CounterFlipFlop counterflipflop_8 (
    .Clock(clock_1_out), .b2(counterflipflop_8_b2), .b1(counterflipflop_8_b1), .b0(counterflipflop_8_b0));
  and and_1 (and_1_out, ~counterflipflop_1_b2, ~counterflipflop_1_b1, ~counterflipflop_1_b0);  // AND_Gate
  and and_2 (and_2_out, ~counterflipflop_2_b2, ~counterflipflop_2_b1, counterflipflop_2_b0);  // AND_Gate
  and and_3 (and_3_out, ~counterflipflop_3_b2, counterflipflop_3_b1, ~counterflipflop_3_b0);  // AND_Gate
  and and_4 (and_4_out, ~counterflipflop_4_b2, counterflipflop_4_b1, counterflipflop_4_b0);  // AND_Gate
  and and_5 (and_5_out, counterflipflop_5_b2, ~counterflipflop_5_b1, ~counterflipflop_5_b0);  // AND_Gate
  and and_6 (and_6_out, counterflipflop_6_b2, ~counterflipflop_6_b1, counterflipflop_6_b0);  // AND_Gate
  and and_7 (and_7_out, counterflipflop_7_b2, counterflipflop_7_b1, ~counterflipflop_7_b0);  // AND_Gate
  and and_8 (and_8_out, counterflipflop_8_b2, counterflipflop_8_b1, counterflipflop_8_b0);
  LED l1 (.in(and_1_out));
  LED l2 (.in(and_2_out));
  LED l3 (.in(and_3_out));
  LED l4 (.in(and_4_out));
  LED l5 (.in(and_5_out));
  LED l6 (.in(and_6_out));
  LED l7 (.in(and_7_out));
  LED l8 (.in(and_8_out));
endmodule

module CounterFlipFlop (
  input  Clock,
  output b2,
  output b1,
  output b0
);

  T_Flip_Flop #(.trigger("falling")) t_ff_1 (.T(1'b1), .clk(Clock), .Q(b0));  // open: Qn, reset, preset
  T_Flip_Flop #(.trigger("falling")) t_ff_2 (.T(1'b1), .clk(b0), .Q(b1));  // open: Qn, reset, preset
  T_Flip_Flop #(.trigger("falling")) t_ff_3 (.T(1'b1), .clk(b1), .Q(b2));  // open: Qn, reset, preset
endmodule

module l4 (
  input  b2,
  input  b1,
  input  b0,
  output l4out
);

  wire and_1_out, and_2_out, and_3_out, and_4_out;

  and and_1 (and_1_out, ~b2, ~b1, ~b0);  // AND_Gate
  and and_2 (and_2_out, b2, ~b1, b0);  // AND_Gate
  and and_3 (and_3_out, b2, b1, ~b0);  // AND_Gate
  and and_4 (and_4_out, b2, b1, b0);
  or or_1 (l4out, and_1_out, and_2_out, and_3_out, and_4_out);
endmodule

module Counter_3bitGameLed (
  output [2:0] out_1
);

  wire and_1_out, and_2_out, and_3_out, clock_1_out, counterflipflop_2_b0, counterflipflop_2_b1,
       counterflipflop_2_b2, counterflipflop_3_b0, counterflipflop_3_b1, counterflipflop_3_b2,
       counterflipflop_4_b0, counterflipflop_4_b1, counterflipflop_4_b2, counterflipflop_5_b0,
       counterflipflop_5_b1, counterflipflop_5_b2, counterflipflop_6_b0, counterflipflop_6_b1,
       counterflipflop_6_b2, counterflipflop_7_b0, counterflipflop_7_b1, counterflipflop_7_b2, l3_1_l3out,
       l4_1_l4out, l5_1_l5out, l6_1_l6out, l7_1_l7out, or_1_out;

  Clock clock_1 (.out(clock_1_out));
  CounterFlipFlop counterflipflop_1 (.Clock(clock_1_out), .b2(out_1[2]), .b1(out_1[1]), .b0(out_1[0]));
  CounterFlipFlop counterflipflop_2 (
    .Clock(clock_1_out), .b2(counterflipflop_2_b2), .b1(counterflipflop_2_b1), .b0(counterflipflop_2_b0));
  CounterFlipFlop counterflipflop_3 (
    .Clock(clock_1_out), .b2(counterflipflop_3_b2), .b1(counterflipflop_3_b1), .b0(counterflipflop_3_b0));
  CounterFlipFlop counterflipflop_4 (
    .Clock(clock_1_out), .b2(counterflipflop_4_b2), .b1(counterflipflop_4_b1), .b0(counterflipflop_4_b0));
  CounterFlipFlop counterflipflop_5 (
    .Clock(clock_1_out), .b2(counterflipflop_5_b2), .b1(counterflipflop_5_b1), .b0(counterflipflop_5_b0));
  CounterFlipFlop counterflipflop_6 (
    .Clock(clock_1_out), .b2(counterflipflop_6_b2), .b1(counterflipflop_6_b1), .b0(counterflipflop_6_b0));
  CounterFlipFlop counterflipflop_7 (
    .Clock(clock_1_out), .b2(counterflipflop_7_b2), .b1(counterflipflop_7_b1), .b0(counterflipflop_7_b0));
  and and_1 (and_1_out, ~counterflipflop_2_b2, ~counterflipflop_2_b1, ~counterflipflop_2_b0);  // AND_Gate
  and and_2 (and_2_out, counterflipflop_2_b2, counterflipflop_2_b1, counterflipflop_2_b0);
  and and_3 (and_3_out, ~out_1[2], ~out_1[1], ~out_1[0]);  // AND_Gate
  or or_1 (or_1_out, and_1_out, and_2_out);
  l3 l3_1 (.b2(counterflipflop_3_b2), .b1(counterflipflop_3_b1), .b0(counterflipflop_3_b0), .l3out(l3_1_l3out));
  l4 l4_1 (.b2(counterflipflop_4_b2), .b1(counterflipflop_4_b1), .b0(counterflipflop_4_b0), .l4out(l4_1_l4out));
  l5 l5_1 (.b2(counterflipflop_5_b2), .b1(counterflipflop_5_b1), .b0(counterflipflop_5_b0), .l5out(l5_1_l5out));
  l6 l6_1 (.b2(counterflipflop_6_b2), .b1(counterflipflop_6_b1), .b0(counterflipflop_6_b0), .l6out(l6_1_l6out));
  l7 l7_1 (.b2(counterflipflop_7_b2), .b1(counterflipflop_7_b1), .b0(counterflipflop_7_b0), .l7out(l7_1_l7out));
  LED l1led (.in(and_3_out));
  LED l2led (.in(or_1_out));
  LED l3led (.in(l3_1_l3out));
  LED l4led (.in(l4_1_l4out));
  LED l5led (.in(l5_1_l5out));
  LED l6led (.in(l6_1_l6out));
  LED l7led (.in(l7_1_l7out));
  LED l8led (.in(1'b1));
endmodule

module l5 (
  input  b2,
  input  b1,
  input  b0,
  output l5out
);

  wire or_1_out, or_2_out, or_3_out;

  or or_1 (or_1_out, b2, b1, ~b0);  // OR_Gate
  or or_2 (or_2_out, b2, ~b1, b0);  // OR_Gate
  or or_3 (or_3_out, b2, ~b1, ~b0);  // OR_Gate
  and and_1 (l5out, or_1_out, or_2_out, or_3_out);
endmodule

module l6 (
  input  b2,
  input  b1,
  input  b0,
  output l6out
);

  wire or_1_out, or_2_out;

  or or_1 (or_1_out, b2, b1, ~b0);  // OR_Gate
  or or_2 (or_2_out, b2, ~b1, b0);  // OR_Gate
  and and_1 (l6out, or_1_out, or_2_out);
endmodule

module l7 (
  input  b2,
  input  b1,
  input  b0,
  output l7out
);

  or or_1 (l7out, b2, b1, ~b0);  // OR_Gate
endmodule

module l3 (
  input  b2,
  input  b1,
  input  b0,
  output l3out
);

  wire and_1_out, and_2_out, and_3_out;

  and and_1 (and_1_out, ~b2, ~b1, ~b0);  // AND_Gate
  and and_2 (and_2_out, b2, b1, ~b0);  // AND_Gate
  and and_3 (and_3_out, b2, b1, b0);
  or or_1 (l3out, and_1_out, and_2_out, and_3_out);
endmodule

module GameLedDecoder (
);

  wire clock_1_out, decoder_1_out0, decoder_1_out1, decoder_1_out2, decoder_1_out3, decoder_1_out4,
       decoder_1_out5, decoder_1_out6, decoder_1_out7;
  wire [2:0] counterflipflop_1_b0;

  Clock clock_1 (.out(clock_1_out));
  CounterFlipFlop counterflipflop_1 (
    .Clock(clock_1_out), .b2(counterflipflop_1_b0[2]), .b1(counterflipflop_1_b0[1]),
    .b0(counterflipflop_1_b0[0]));
  Decoder #(.select(3)) decoder_1 (
    .out0(decoder_1_out0), .out1(decoder_1_out1), .out2(decoder_1_out2), .out3(decoder_1_out3),
    .out4(decoder_1_out4), .out5(decoder_1_out5), .out6(decoder_1_out6), .out7(decoder_1_out7),
    .sel(counterflipflop_1_b0));  // open: en
  LED led_1 (.in(decoder_1_out0));
  LED led_2 (.in(decoder_1_out1));
  LED led_3 (.in(decoder_1_out2));
  LED led_4 (.in(decoder_1_out3));
  LED led_5 (.in(decoder_1_out4));
  LED led_6 (.in(decoder_1_out5));
  LED led_7 (.in(decoder_1_out6));
  LED led_8 (.in(decoder_1_out7));
endmodule
