// Logisim project mem8bit.circ as structural Verilog: 2 circuits, main circuit DFlipFlop
module DFlipFlop (
  input  Set,
  input  Reset,
  input  D,
  input  CLOCK,
  output Q,
  output QNeg
);

  wire and_1_out, and_2_out, nand_1_out, nand_2_out, nand_3_out, nand_4_out, not_1_out;

  not not_1 (not_1_out, D);
  nand nand_1 (nand_1_out, D, CLOCK);
  nand nand_2 (nand_2_out, CLOCK, not_1_out);
  nand nand_3 (nand_3_out, nand_1_out, nand_4_out);
  nand nand_4 (nand_4_out, nand_3_out, nand_2_out);
  // Probe on nand_3_out
  // Probe on nand_4_out
  and and_1 (and_1_out, Set, ~Reset);  // AND_Gate
  and and_2 (and_2_out, ~Reset, nand_3_out);  // AND_Gate
  or or_1 (Q, and_1_out, and_2_out);
  not not_2 (QNeg, Q);
endmodule

module Registro8Bit (
  input  [7:0] D,
  input  Set,
  input  Reset,
  input  CLOCK,
  output [7:0] Q,
  output [7:0] QNeg
);

  // Probe on D
  DFlipFlop dflipflop_1 (.Set(Set), .Reset(Reset), .D(D[0]), .CLOCK(CLOCK), .Q(Q[0]), .QNeg(QNeg[0]));
  DFlipFlop dflipflop_2 (.Set(Set), .Reset(Reset), .D(D[1]), .CLOCK(CLOCK), .Q(Q[1]), .QNeg(QNeg[1]));
  DFlipFlop dflipflop_3 (.Set(Set), .Reset(Reset), .D(D[2]), .CLOCK(CLOCK), .Q(Q[2]), .QNeg(QNeg[2]));
  DFlipFlop dflipflop_4 (.Set(Set), .Reset(Reset), .D(D[3]), .CLOCK(CLOCK), .Q(Q[3]), .QNeg(QNeg[3]));
  DFlipFlop dflipflop_5 (.Set(Set), .Reset(Reset), .D(D[4]), .CLOCK(CLOCK), .Q(Q[4]), .QNeg(QNeg[4]));
  DFlipFlop dflipflop_6 (.Set(Set), .Reset(Reset), .D(D[5]), .CLOCK(CLOCK), .Q(Q[5]), .QNeg(QNeg[5]));
  DFlipFlop dflipflop_7 (.Set(Set), .Reset(Reset), .D(D[6]), .CLOCK(CLOCK), .Q(Q[6]), .QNeg(QNeg[6]));
  DFlipFlop dflipflop_8 (.Set(Set), .Reset(Reset), .D(D[7]), .CLOCK(CLOCK), .Q(Q[7]), .QNeg(QNeg[7]));
  // Probe on Q
  // Probe on QNeg
endmodule
